// Logisim project control.circ as structural Verilog: 1 circuit, main circuit control
module control (
  input  go,
  input  isControl32,
  input  Product0,
  input  Clock,
  output Load_Multiplicand,
  output Load_Product,
  output Op_Select,
  output Increment_Counter
);

  wire and_1_out, and_2_out, and_3_out, and_4_out, and_5_out, and_6_out, and_7_out, and_8_out, and_9_out,
       not_1_out, not_2_out, not_3_out, not_4_out, not_5_out, not_6_out, not_7_out, not_8_out, not_9_out,
       not_10_out, not_11_out, not_12_out, not_13_out, not_14_out, not_15_out, not_16_out, not_17_out,
       not_18_out, not_19_out, not_20_out, not_21_out, not_22_out, not_23_out, not_24_out, not_25_out, S4_out;
  wire [2:0] _3_bit_State_Register_q, n0_out;

  Register #(.width(3)) _3_bit_State_Register (.D(n0_out), .Q(_3_bit_State_Register_q), .clk(Clock));  // open: en, clr
  not not_1 (not_1_out, _3_bit_State_Register_q[2]);
  not not_2 (not_2_out, _3_bit_State_Register_q[0]);
  not not_3 (not_3_out, Product0);
  not not_4 (not_4_out, _3_bit_State_Register_q[1]);
  not not_5 (not_5_out, _3_bit_State_Register_q[0]);
  not not_6 (not_6_out, _3_bit_State_Register_q[2]);
  not not_7 (not_7_out, _3_bit_State_Register_q[2]);
  not not_8 (not_8_out, _3_bit_State_Register_q[1]);
  not not_9 (not_9_out, _3_bit_State_Register_q[2]);
  not not_10 (not_10_out, _3_bit_State_Register_q[0]);
  not not_11 (not_11_out, _3_bit_State_Register_q[1]);
  not not_12 (not_12_out, isControl32);
  not not_13 (not_13_out, _3_bit_State_Register_q[2]);
  not not_14 (not_14_out, _3_bit_State_Register_q[1]);
  not not_15 (not_15_out, _3_bit_State_Register_q[0]);
  not not_16 (not_16_out, _3_bit_State_Register_q[2]);
  not not_17 (not_17_out, _3_bit_State_Register_q[0]);
  not not_18 (not_18_out, _3_bit_State_Register_q[1]);
  not not_19 (not_19_out, _3_bit_State_Register_q[0]);
  not not_20 (not_20_out, _3_bit_State_Register_q[2]);
  not not_21 (not_21_out, _3_bit_State_Register_q[1]);
  not not_22 (not_22_out, _3_bit_State_Register_q[2]);
  not not_23 (not_23_out, _3_bit_State_Register_q[1]);
  not not_24 (not_24_out, _3_bit_State_Register_q[0]);
  not not_25 (not_25_out, _3_bit_State_Register_q[1]);
  and and_1 (and_1_out, not_1_out, _3_bit_State_Register_q[1], not_2_out, not_3_out);
  and and_2 (and_2_out, _3_bit_State_Register_q[2], not_4_out, not_5_out);
  and and_3 (and_3_out, not_6_out, _3_bit_State_Register_q[1], _3_bit_State_Register_q[0]);
  and and_4 (and_4_out, not_7_out, not_8_out, _3_bit_State_Register_q[0]);
  and and_5 (and_5_out, not_9_out, _3_bit_State_Register_q[1], not_10_out, Product0);
  and and_6 (and_6_out, _3_bit_State_Register_q[2], not_11_out, _3_bit_State_Register_q[0], not_12_out);
  and and_7 (and_7_out, not_13_out, not_14_out, not_15_out, go);
  and and_8 (and_8_out, not_16_out, _3_bit_State_Register_q[1], not_17_out, Product0);
  and and_9 (and_9_out, _3_bit_State_Register_q[2], not_18_out, not_19_out);
  and S1 (Load_Multiplicand, not_20_out, not_21_out, _3_bit_State_Register_q[0]);
  and S3 (Op_Select, not_22_out, _3_bit_State_Register_q[1], _3_bit_State_Register_q[0]);
  and S4 (S4_out, _3_bit_State_Register_q[2], not_23_out, not_24_out);
  and S5 (Increment_Counter, _3_bit_State_Register_q[2], not_25_out, _3_bit_State_Register_q[0]);
  or n2 (n0_out[2], and_1_out, and_2_out, and_3_out);
  or n1 (n0_out[1], and_4_out, and_5_out, and_6_out);
  or n0 (n0_out[0], and_7_out, and_8_out, and_9_out);
  or or_1 (Load_Product, Load_Multiplicand, Op_Select, S4_out);
endmodule
