// Logisim project datapath.circ as structural Verilog: 4 circuits, main circuit datapath
module datapath (
  input  Op_Select,
  input  Load_Multiplicand,
  input  Increment_Counter,
  input  Load_Product,
  input  [31:0] Multiplier,
  input  [31:0] Multiplicand,
  input  Clock,
  output isCounter32,
  output [31:0] Product_63_32,
  output [31:0] Product_31_0,
  output Product0
);

  wire [4:0] counter_q;
  wire [31:0] multiplexer_1_out, Multiplicand_q, n32bit_alu_1_resul_31_0, n32bit_alu_1_result_63_32;

  Counter #(.width(5), .max('h1f)) counter (
    .count(Increment_Counter), .Q(counter_q), .clk(Clock), .clr(Load_Multiplicand));  // open: load, D, carry
  Register #(.width(32)) u_Product_63_32 (
    .D(n32bit_alu_1_result_63_32), .en(Load_Product), .Q(Product_63_32), .clk(Clock), .clr(Load_Multiplicand));
  Multiplexer #(.width(32), .enable("false")) multiplexer_1 (
    .in0(n32bit_alu_1_resul_31_0), .in1(Multiplier), .out(multiplexer_1_out), .sel(Load_Multiplicand));
  Register #(.width(32)) u_Product_31_0 (
    .D(multiplexer_1_out), .en(Load_Product), .Q({Product_31_0[31:1], Product0}), .clk(Clock));  // open: clr
  Register #(.width(32)) u_Multiplicand (
    .D(Multiplicand), .en(Load_Multiplicand), .Q(Multiplicand_q), .clk(Clock));  // open: clr
  _32bit_ALU u_32bit_alu_1 (
    .OP_Select(Op_Select), .Multiplicand(Multiplicand_q), ._63_32(Product_63_32),
    ._31_0({Product_31_0[31:1], Product0}), .Result_63_32(n32bit_alu_1_result_63_32),
    .Resul_31_0(n32bit_alu_1_resul_31_0));
  and and_1 (isCounter32, counter_q[0], counter_q[1], counter_q[2], counter_q[3], counter_q[4]);

  assign Product_31_0[0] = Product0;
endmodule

module _32bit_ALU (
  input  OP_Select,
  input  [31:0] Multiplicand,
  input  [31:0] _63_32,
  input  [31:0] _31_0,
  output [31:0] Result_63_32,
  output [31:0] Resul_31_0
);

  wire [31:0] _32bit_Adder_result;

  _32bit_Adder _32bit_Adder (.A(_63_32), .B(Multiplicand), .Result(_32bit_Adder_result));
  Multiplexer #(.width(32), .enable("false")) multiplexer_1 (
    .in0({1'b0, _63_32[31:1]}), .in1(_32bit_Adder_result), .out(Result_63_32), .sel(OP_Select));
  Multiplexer #(.width(32), .enable("false")) multiplexer_2 (
    .in0({_63_32[0], _31_0[31:1]}), .in1(_31_0), .out(Resul_31_0), .sel(OP_Select));
endmodule

module _32bit_Adder (
  input  [31:0] A,
  input  [31:0] B,
  output [31:0] Result
);

  wire n1bit_adder_2_c_i_1, n1bit_adder_3_c_i_1, n1bit_adder_4_c_i_1, n1bit_adder_5_c_i_1,
       n1bit_adder_6_c_i_1, n1bit_adder_7_c_i_1, n1bit_adder_8_c_i_1, n1bit_adder_9_c_i_1,
       n1bit_adder_10_c_i_1, n1bit_adder_11_c_i_1, n1bit_adder_12_c_i_1, n1bit_adder_13_c_i_1,
       n1bit_adder_14_c_i_1, n1bit_adder_15_c_i_1, n1bit_adder_16_c_i_1, n1bit_adder_17_c_i_1,
       n1bit_adder_18_c_i_1, n1bit_adder_19_c_i_1, n1bit_adder_20_c_i_1, n1bit_adder_21_c_i_1,
       n1bit_adder_22_c_i_1, n1bit_adder_23_c_i_1, n1bit_adder_24_c_i_1, n1bit_adder_25_c_i_1,
       n1bit_adder_26_c_i_1, n1bit_adder_27_c_i_1, n1bit_adder_28_c_i_1, n1bit_adder_29_c_i_1,
       n1bit_adder_30_c_i_1, n1bit_adder_31_c_i_1, n1bit_adder_32_c_i_1;

  _1bit_Adder u_1bit_adder_1 (.b_i(B[31]), .a_i(A[31]), .r_i(Result[31]), .c_i(n1bit_adder_2_c_i_1));  // open: c_i_1
  _1bit_Adder u_1bit_adder_2 (
    .c_i_1(n1bit_adder_2_c_i_1), .b_i(B[30]), .a_i(A[30]), .r_i(Result[30]), .c_i(n1bit_adder_3_c_i_1));
  _1bit_Adder u_1bit_adder_3 (
    .c_i_1(n1bit_adder_3_c_i_1), .b_i(B[29]), .a_i(A[29]), .r_i(Result[29]), .c_i(n1bit_adder_4_c_i_1));
  _1bit_Adder u_1bit_adder_4 (
    .c_i_1(n1bit_adder_4_c_i_1), .b_i(B[28]), .a_i(A[28]), .r_i(Result[28]), .c_i(n1bit_adder_5_c_i_1));
  _1bit_Adder u_1bit_adder_5 (
    .c_i_1(n1bit_adder_5_c_i_1), .b_i(B[27]), .a_i(A[27]), .r_i(Result[27]), .c_i(n1bit_adder_6_c_i_1));
  _1bit_Adder u_1bit_adder_6 (
    .c_i_1(n1bit_adder_6_c_i_1), .b_i(B[26]), .a_i(A[26]), .r_i(Result[26]), .c_i(n1bit_adder_7_c_i_1));
  _1bit_Adder u_1bit_adder_7 (
    .c_i_1(n1bit_adder_7_c_i_1), .b_i(B[25]), .a_i(A[25]), .r_i(Result[25]), .c_i(n1bit_adder_8_c_i_1));
  _1bit_Adder u_1bit_adder_8 (
    .c_i_1(n1bit_adder_8_c_i_1), .b_i(B[24]), .a_i(A[24]), .r_i(Result[24]), .c_i(n1bit_adder_9_c_i_1));
  _1bit_Adder u_1bit_adder_9 (
    .c_i_1(n1bit_adder_9_c_i_1), .b_i(B[23]), .a_i(A[23]), .r_i(Result[23]), .c_i(n1bit_adder_11_c_i_1));
  _1bit_Adder u_1bit_adder_10 (
    .c_i_1(n1bit_adder_10_c_i_1), .b_i(B[21]), .a_i(A[21]), .r_i(Result[21]), .c_i(n1bit_adder_12_c_i_1));
  _1bit_Adder u_1bit_adder_11 (
    .c_i_1(n1bit_adder_11_c_i_1), .b_i(B[22]), .a_i(A[22]), .r_i(Result[22]), .c_i(n1bit_adder_10_c_i_1));
  _1bit_Adder u_1bit_adder_12 (
    .c_i_1(n1bit_adder_12_c_i_1), .b_i(B[20]), .a_i(A[20]), .r_i(Result[20]), .c_i(n1bit_adder_13_c_i_1));
  _1bit_Adder u_1bit_adder_13 (
    .c_i_1(n1bit_adder_13_c_i_1), .b_i(B[19]), .a_i(A[19]), .r_i(Result[19]), .c_i(n1bit_adder_14_c_i_1));
  _1bit_Adder u_1bit_adder_14 (
    .c_i_1(n1bit_adder_14_c_i_1), .b_i(B[18]), .a_i(A[18]), .r_i(Result[18]), .c_i(n1bit_adder_15_c_i_1));
  _1bit_Adder u_1bit_adder_15 (
    .c_i_1(n1bit_adder_15_c_i_1), .b_i(B[17]), .a_i(A[17]), .r_i(Result[17]), .c_i(n1bit_adder_17_c_i_1));
  _1bit_Adder u_1bit_adder_16 (
    .c_i_1(n1bit_adder_16_c_i_1), .b_i(B[15]), .a_i(A[15]), .r_i(Result[15]), .c_i(n1bit_adder_18_c_i_1));
  _1bit_Adder u_1bit_adder_17 (
    .c_i_1(n1bit_adder_17_c_i_1), .b_i(B[16]), .a_i(A[16]), .r_i(Result[16]), .c_i(n1bit_adder_16_c_i_1));
  _1bit_Adder u_1bit_adder_18 (
    .c_i_1(n1bit_adder_18_c_i_1), .b_i(B[14]), .a_i(A[14]), .r_i(Result[14]), .c_i(n1bit_adder_19_c_i_1));
  _1bit_Adder u_1bit_adder_19 (
    .c_i_1(n1bit_adder_19_c_i_1), .b_i(B[13]), .a_i(A[13]), .r_i(Result[13]), .c_i(n1bit_adder_21_c_i_1));
  _1bit_Adder u_1bit_adder_20 (
    .c_i_1(n1bit_adder_20_c_i_1), .b_i(B[11]), .a_i(A[11]), .r_i(Result[11]), .c_i(n1bit_adder_22_c_i_1));
  _1bit_Adder u_1bit_adder_21 (
    .c_i_1(n1bit_adder_21_c_i_1), .b_i(B[12]), .a_i(A[12]), .r_i(Result[12]), .c_i(n1bit_adder_20_c_i_1));
  _1bit_Adder u_1bit_adder_22 (
    .c_i_1(n1bit_adder_22_c_i_1), .b_i(B[10]), .a_i(A[10]), .r_i(Result[10]), .c_i(n1bit_adder_23_c_i_1));
  _1bit_Adder u_1bit_adder_23 (
    .c_i_1(n1bit_adder_23_c_i_1), .b_i(B[9]), .a_i(A[9]), .r_i(Result[9]), .c_i(n1bit_adder_24_c_i_1));
  _1bit_Adder u_1bit_adder_24 (
    .c_i_1(n1bit_adder_24_c_i_1), .b_i(B[8]), .a_i(A[8]), .r_i(Result[8]), .c_i(n1bit_adder_25_c_i_1));
  _1bit_Adder u_1bit_adder_25 (
    .c_i_1(n1bit_adder_25_c_i_1), .b_i(B[7]), .a_i(A[7]), .r_i(Result[7]), .c_i(n1bit_adder_27_c_i_1));
  _1bit_Adder u_1bit_adder_26 (
    .c_i_1(n1bit_adder_26_c_i_1), .b_i(B[5]), .a_i(A[5]), .r_i(Result[5]), .c_i(n1bit_adder_29_c_i_1));
  _1bit_Adder u_1bit_adder_27 (
    .c_i_1(n1bit_adder_27_c_i_1), .b_i(B[6]), .a_i(A[6]), .r_i(Result[6]), .c_i(n1bit_adder_26_c_i_1));
  _1bit_Adder u_1bit_adder_28 (
    .c_i_1(n1bit_adder_28_c_i_1), .b_i(B[3]), .a_i(A[3]), .r_i(Result[3]), .c_i(n1bit_adder_30_c_i_1));
  _1bit_Adder u_1bit_adder_29 (
    .c_i_1(n1bit_adder_29_c_i_1), .b_i(B[4]), .a_i(A[4]), .r_i(Result[4]), .c_i(n1bit_adder_28_c_i_1));
  _1bit_Adder u_1bit_adder_30 (
    .c_i_1(n1bit_adder_30_c_i_1), .b_i(B[2]), .a_i(A[2]), .r_i(Result[2]), .c_i(n1bit_adder_31_c_i_1));
  _1bit_Adder u_1bit_adder_31 (
    .c_i_1(n1bit_adder_31_c_i_1), .b_i(B[1]), .a_i(A[1]), .r_i(Result[1]), .c_i(n1bit_adder_32_c_i_1));
  _1bit_Adder u_1bit_adder_32 (.c_i_1(n1bit_adder_32_c_i_1), .b_i(B[0]), .a_i(A[0]), .r_i(Result[0]), .c_i(1'b0));
endmodule

module _1bit_Adder (
  input  b_i,
  input  a_i,
  input  c_i,
  output c_i_1,
  output r_i
);

  wire and_1_out, and_2_out, and_3_out, not_1_out, not_2_out, or_2_out, or_3_out;

  or or_1 (c_i_1, and_1_out, and_3_out);
  and and_1 (and_1_out, a_i, b_i);
  not not_1 (not_1_out, and_1_out);
  or or_2 (or_2_out, b_i, a_i);
  and and_2 (and_2_out, not_1_out, or_2_out);
  and and_3 (and_3_out, and_2_out, c_i);
  not not_2 (not_2_out, and_3_out);
  and and_4 (r_i, not_2_out, or_3_out);
  or or_3 (or_3_out, and_2_out, c_i);
endmodule
