// Logisim project mult32.circ as structural Verilog: 1 circuit, main circuit mult32
module mult32 (
  input  [31:0] Multiplier,
  input  [31:0] Multiplicand,
  output [31:0] HI,
  output [31:0] LO
);

  wire Button_out, clock_1_out, control_1_increment_counter, control_1_load_multiplicand,
       control_1_load_product, control_1_op_select, datapath_1_iscounter32, datapath_1_product0;

  Button Button (.out(Button_out));
  Clock clock_1 (.out(clock_1_out));
  control control_1 (
    .go(Button_out), .isControl32(datapath_1_iscounter32), .Product0(datapath_1_product0),
    .Clock(clock_1_out), .Load_Multiplicand(control_1_load_multiplicand),
    .Load_Product(control_1_load_product), .Op_Select(control_1_op_select),
    .Increment_Counter(control_1_increment_counter));
  datapath datapath_1 (
    .Op_Select(control_1_op_select), .Load_Multiplicand(control_1_load_multiplicand),
    .Increment_Counter(control_1_increment_counter), .Load_Product(control_1_load_product),
    .Multiplier(Multiplier), .Multiplicand(Multiplicand), .Clock(clock_1_out),
    .isCounter32(datapath_1_iscounter32), .Product_63_32(HI), .Product_31_0(LO),
    .Product0(datapath_1_product0));
endmodule
